# Fritzing sketch buzzer (saved by Fritzing 0.4.3b)
breadboards: 1

parts:
  R1 = Resistor [resistance=220 package=THT]
  J1 = Piezo Speaker
  Arduino1 = Arduino

nets:
  N1: R1.Pin_0, Arduino1.D9
  N2: R1.Pin_1, J1.pin1, Arduino1.GND
  N3: J1.pin2, Arduino1.D2
