# Fritzing sketch digital-output-loop_Loop (saved by Fritzing 0.3.2b)
breadboards: 1

parts:
  LED1 = Red LED - 5mm
  R1 = 220 Ω Resistor [package=THT]
  LED2 = Red LED - 5mm
  R2 = 220 Ω Resistor [package=THT]
  LED3 = Red LED - 5mm
  R3 = 220 Ω Resistor [package=THT]
  LED4 = Red LED - 5mm
  R4 = 220 Ω Resistor [package=THT]
  LED5 = Red LED - 5mm
  R5 = 220 Ω Resistor [package=THT]
  LED6 = Red LED - 5mm
  R6 = 220 Ω Resistor [package=THT]
  Arduino2 = Arduino

nets:
  N1: LED1.cathode, LED2.cathode, LED3.cathode, LED4.cathode, LED5.cathode, LED6.cathode, Arduino2.GND
  N2: LED1.anode, R1.Pin_0
  N3: R1.Pin_1, Arduino2.D7
  N4: LED2.anode, R2.Pin_0
  N5: R2.Pin_1, Arduino2.D6
  N6: LED3.anode, R3.Pin_0
  N7: R3.Pin_1, Arduino2.D5
  N8: LED4.anode, R4.Pin_0
  N9: R4.Pin_1, Arduino2.D4
  N10: LED5.anode, R5.Pin_0
  N11: R5.Pin_1, Arduino2.D3
  N12: LED6.anode, R6.Pin_0
  N13: R6.Pin_1, Arduino2.D2

notes:
  In this example, six leds are controlled by digital out pins. Related Example: http://arduino.cc/en/Tutorial/Loop
