# Fritzing sketch analog-inputoutput_AnalogInputOutput (saved by Fritzing 0.3.2b)
breadboards: 1

parts:
  LED1 = Red LED - 5mm
  R2 = 220 Ω Resistor [package=THT]
  R3 = Rotary Potentiometer (Large) [package=THT]
  Arduino2 = Arduino

nets:
  N1: LED1.cathode, R3.leg2, Arduino2.GND
  N2: LED1.anode, R2.Pin_0
  N3: R2.Pin_1, Arduino2.D3
  N4: R3.leg1, Arduino2.+5V
  N5: R3.wiper, Arduino2.A3

notes:
  In this example, potentiometer values are read in through an 'Analog In' pin. The values are then used to control the modulation of an LED on a PWM pin. Related examples: http://arduino.cc/en/Tutorial/AnalogInput http://arduino.cc/en/Tutorial/Fading
