# Fritzing sketch analog-input-thermistor_AnalogInputThermistor (saved by Fritzing 0.3.2b)
breadboards: 1

parts:
  R1 = Temperature Sensor (Thermistor) [package=THT]
  R2 = 1k Ω Resistor [package=THT]
  LED1 = Blue LED - 5mm
  Arduino2 = Arduino

nets:
  N1: R1.pin_0, Arduino2.+5V
  N2: R1.pin_1, R2.Pin_1, Arduino2.A2
  N3: R2.Pin_0, LED1.cathode, Arduino2.GND
  N4: LED1.anode, Arduino2.D13

notes:
  In this example, thermistor values are read in through an 'Analog In' pin. The values are then used to control the blinking rate of an LED.
  Using a multimeter, check the min and max resistance of the thermistor in different light conditions. Then calculate the resistor's value with the Axel-Benz formula: Rref = sqrt(Rmin*Rmax)
  Related example: http://arduino.cc/en/Tutorial/AnalogInput
